// Logisim project control_logic.circ as structural Verilog: 14 circuits, main circuit control_logic
module control_logic (
  input  [31:0] inst,
  input  BrEq,
  input  BrLt,
  output PCSel,
  output RegWEn,
  output [2:0] ImmSel,
  output BrUn,
  output ASel,
  output BSel,
  output [3:0] ALUSel,
  output MemRW,
  output [1:0] WBSel,
  output CSRSel,
  output CSRWen,
  output [1:0] out_15
);

  wire IsAuipc, IsBType, IsIType, IsJal, IsJalr, IsLoadType, IsLui, IsRType, or_3_out, or_4_out, or_5_out,
       or_6_out, or_7_out, or_8_out;

  ITypeDetector itypedetector_1 (.out_2(IsIType), .in_1(inst[6:0]));
  or or_1 (RegWEn, IsIType, IsRType, IsLoadType, IsLui, IsAuipc, IsJal, IsJalr);
  or or_2 (ASel, IsBType, IsAuipc, IsJal);
  or or_3 (or_3_out, IsIType, IsRType, IsLui, IsAuipc);
  or or_4 (or_4_out, IsJal, IsJalr);
  RTypeDetector rtypedetector_1 (.in_1(inst[6:0]), .out_2(IsRType));
  LoadTypeDetector loadtypedetector_1 (.in_1(inst[6:0]), .out_2(IsLoadType));
  STypeDetector stypedetector_1 (.in_1(inst[6:0]), .out_2(MemRW));
  BTypeDetector btypedetector_1 (.in_1(inst[6:0]), .out_2(IsBType));
  LuiDetector luidetector_1 (.in_1(inst[6:0]), .out_2(IsLui));
  AuipcDetector auipcdetector_1 (.in_1(inst[6:0]), .out_2(IsAuipc));
  JalDetector jaldetector_1 (.in_1(inst[6:0]), .out_2(IsJal));
  JalrDetector jalrdetector_1 (.in_1(inst[6:0]), .out_2(IsJalr));
  CSRTypeDetector csrtypedetector_1 (.in_1(inst[6:0]), .out_2(CSRWen));
  Priority_Encoder #(.select(2)) priority_encoder_1 (
    .in0(or_3_out), .in1(IsLoadType), .in2(or_4_out), .out(WBSel));  // open: in3, gs, en_out, en_in
  and and_1 (CSRSel, CSRWen, inst[12], ~inst[13], inst[14]);  // AND_Gate
  or or_5 (or_5_out, IsLoadType, MemRW, IsBType, IsAuipc, IsJal, IsJalr);
  or or_6 (or_6_out, IsJal, IsJalr);
  or or_7 (or_7_out, IsIType, IsLoadType, IsJalr);
  or or_8 (or_8_out, IsLui, IsAuipc);
  ALUSelGenerator aluselgenerator_1 (
    .out_7(ALUSel), .in_1(inst[14:12]), .in_2(inst[31:25]), .in_3(IsIType), .in_4(IsRType), .in_5(or_5_out),
    .in_6(IsLui));
  and and_2 (BrUn, IsBType, inst[13], inst[14]);
  Priority_Encoder priority_encoder_2 (
    .in0(or_7_out), .in1(MemRW), .in2(IsBType), .in3(or_8_out), .in4(IsJal), .in5(CSRWen), .out(ImmSel));  // open: in6, in7, en_in, gs, en_out
  or or_9 (BSel, IsIType, IsLoadType, MemRW, IsBType, IsLui, IsAuipc, IsJal, IsJalr);
  MaskGenerator maskgenerator_1 (.in_1(inst[14:12]), .in_2(IsLoadType), .in_3(MemRW), .out_4(out_15));
  PCSelGenerator pcselgenerator_1 (
    .in_1(inst[14:12]), .in_2(IsBType), .BrEq(BrEq), .BrLt(BrLt), .in_5(or_6_out), .out_6(PCSel));

  // Other names for the same wires on the sheet: OpCode[6:0] = inst[6:0]; Func3[2:0] = inst[14:12];
  //   Func7[6:0] = inst[31:25]; IsCSRType = CSRWen; IsSType = MemRW; MaskType[1:0] = out_15

  // Notes on the sheet:
  //   INPUTS to your circuit
  //   DON'T CHANGE THE LOCATIONS OF THE INPUTS AND OUTPUTS!
  //   OUTPUT from your circuit
endmodule

module ITypeDetector (
  input  [6:0] in_1,
  output out_2
);

  and and_1 (out_2, in_1[0], in_1[1], ~in_1[2], ~in_1[3], in_1[4], ~in_1[5], ~in_1[6]);  // AND_Gate

  // Other names for the same wires on the sheet: IsIType = out_2; OpCode[6:0] = in_1

  // Notes on the sheet:
  //   input
  //   output
endmodule

module ALUSelGenerator (
  input  [2:0] in_1,
  input  [6:0] in_2,
  input  in_3,
  input  in_4,
  input  in_5,
  input  in_6,
  output [3:0] out_7
);

  wire add0, and1, and_1_out, and_2_out, and_3_out, and_4_out, and_9_out, and_10_out, and_11_out, and_12_out,
       and_14_out, and_15_out, mul10, mulh14, mulhu11, or2, or_1_out, or_2_out, or_5_out, sll6, slt7, sra5,
       srl4, sub12, xor3;

  or or_1 (or_1_out, in_3, in_4);
  and and_1 (and_1_out, ~in_1[0], ~in_1[1], ~in_1[2], ~in_2[0], ~in_2[5], in_4);  // AND_Gate
  and and_2 (and_2_out, ~in_1[0], ~in_1[1], ~in_1[2], in_3);  // AND_Gate
  and and_3 (and_3_out, ~in_1[0], in_1[1], in_1[2], ~in_2[0], ~in_2[5], in_4);  // AND_Gate
  and and_4 (and_4_out, ~in_1[0], in_1[1], in_1[2], in_3);  // AND_Gate
  or or_2 (or_2_out, in_3, in_4);
  and and_5 (srl4, in_1[0], ~in_1[1], in_1[2], ~in_2[0], ~in_2[5], or_2_out);  // AND_Gate
  and and_6 (sll6, in_1[0], ~in_1[1], ~in_1[2], ~in_2[0], ~in_2[5], or_1_out);  // AND_Gate
  and and_7 (mul10, ~in_1[0], ~in_1[1], ~in_1[2], in_2[0], ~in_2[5], in_4);  // AND_Gate
  and and_8 (sub12, ~in_1[0], ~in_1[1], ~in_1[2], ~in_2[0], in_2[5], in_4);  // AND_Gate
  or or_3 (add0, and_1_out, and_2_out, in_5);
  or or_4 (or2, and_3_out, and_4_out);
  or or_5 (or_5_out, in_3, in_4);
  and and_9 (and_9_out, in_1[0], in_1[1], in_1[2], ~in_2[5], in_4);  // AND_Gate
  and and_10 (and_10_out, in_1[0], in_1[1], in_1[2], in_3);
  and and_11 (and_11_out, ~in_1[0], ~in_1[1], in_1[2], ~in_2[0], ~in_2[5], in_4);  // AND_Gate
  and and_12 (and_12_out, ~in_1[0], ~in_1[1], in_1[2], in_3);  // AND_Gate
  and and_13 (sra5, in_1[0], ~in_1[1], in_1[2], ~in_2[0], in_2[5], or_5_out);  // AND_Gate
  and and_14 (and_14_out, ~in_1[0], in_1[1], ~in_1[2], ~in_2[0], ~in_2[5], in_4);  // AND_Gate
  and and_15 (and_15_out, ~in_1[0], in_1[1], ~in_1[2], in_3);  // AND_Gate
  and and_16 (mulhu11, in_1[0], in_1[1], ~in_1[2], in_2[0], ~in_2[5], in_4);  // AND_Gate
  and and_17 (mulh14, in_1[0], ~in_1[1], ~in_1[2], in_2[0], ~in_2[5], in_4);  // AND_Gate
  or or_6 (and1, and_9_out, and_10_out);
  or or_7 (xor3, and_11_out, and_12_out);
  or or_8 (slt7, and_14_out, and_15_out);
  Priority_Encoder #(.select(4)) priority_encoder_1 (
    .in0(add0), .in1(and1), .in2(or2), .in3(xor3), .in4(srl4), .in5(sra5), .in6(sll6), .in7(slt7),
    .in10(mul10), .in11(mulhu11), .in12(sub12), .in13(in_6), .in14(mulh14), .out(out_7), .en_in(1'b1));  // open: in8, in9, in15, gs, en_out

  // Other names for the same wires on the sheet: ALUSel[3:0] = out_7; Func3[2:0] = in_1; Func7[6:0] = in_2;
  //   IsAddType = in_5; IsIType = in_3; IsRType = in_4; SelectB = in_6

  // Notes on the sheet:
  //   input
  //   output
endmodule

module RTypeDetector (
  input  [6:0] in_1,
  output out_2
);

  and and_1 (out_2, in_1[0], in_1[1], ~in_1[2], ~in_1[3], in_1[4], in_1[5], ~in_1[6]);  // AND_Gate

  // Other names for the same wires on the sheet: IsRType = out_2; OpCode[6:0] = in_1

  // Notes on the sheet:
  //   input
  //   output
endmodule

module LoadTypeDetector (
  input  [6:0] in_1,
  output out_2
);

  and and_1 (out_2, in_1[0], in_1[1], ~in_1[2], ~in_1[3], ~in_1[4], ~in_1[5], ~in_1[6]);  // AND_Gate

  // Other names for the same wires on the sheet: IsLoadType = out_2; OpCode[6:0] = in_1

  // Notes on the sheet:
  //   input
  //   output
endmodule

module MaskGenerator (
  input  [2:0] in_1,
  input  in_2,
  input  in_3,
  output [1:0] out_4
);

  wire ByteMask, HalfMask, or_1_out, or_2_out, or_3_out, WordMask;

  or or_1 (or_1_out, in_2, in_3);
  or or_2 (or_2_out, in_2, in_3);
  or or_3 (or_3_out, in_2, in_3);
  and and_1 (ByteMask, ~in_1[0], ~in_1[1], ~in_1[2], or_1_out);  // AND_Gate
  and and_2 (HalfMask, in_1[0], ~in_1[1], ~in_1[2], or_2_out);  // AND_Gate
  and and_3 (WordMask, ~in_1[0], in_1[1], ~in_1[2], or_3_out);  // AND_Gate
  Priority_Encoder #(.select(2)) priority_encoder_1 (
    .in0(1'b1), .in1(ByteMask), .in2(HalfMask), .in3(WordMask), .out(out_4));  // open: gs, en_out, en_in

  // Other names for the same wires on the sheet: Func3[2:0] = in_1; isLoadType = in_2; isSType = in_3;
  //   MaskType[1:0] = out_4

  // Notes on the sheet:
  //   input
  //   output
endmodule

module STypeDetector (
  input  [6:0] in_1,
  output out_2
);

  and and_1 (out_2, in_1[0], in_1[1], ~in_1[2], ~in_1[3], ~in_1[4], in_1[5], ~in_1[6]);  // AND_Gate

  // Other names for the same wires on the sheet: IsSType = out_2; OpCode[6:0] = in_1

  // Notes on the sheet:
  //   input
  //   output
endmodule

module BTypeDetector (
  input  [6:0] in_1,
  output out_2
);

  and and_1 (out_2, in_1[0], in_1[1], ~in_1[2], ~in_1[3], ~in_1[4], in_1[5], in_1[6]);  // AND_Gate

  // Other names for the same wires on the sheet: IsBType = out_2; OpCode[6:0] = in_1

  // Notes on the sheet:
  //   input
  //   output
endmodule

module PCSelGenerator (
  input  [2:0] in_1,
  input  in_2,
  input  BrEq,
  input  BrLt,
  input  in_5,
  output out_6
);

  wire beq, bge, bgeu, blt, bltu, bne, not_1_out, not_2_out;
  wire [2:0] priority_encoder_1_out;

  and and_1 (beq, ~in_1[0], ~in_1[1], ~in_1[2], in_2);  // AND_Gate
  and and_2 (bne, in_1[0], ~in_1[1], ~in_1[2], in_2);  // AND_Gate
  and and_3 (blt, ~in_1[0], ~in_1[1], in_1[2], in_2);  // AND_Gate
  and and_4 (bge, in_1[0], ~in_1[1], in_1[2], in_2);  // AND_Gate
  and and_5 (bltu, ~in_1[0], in_1[1], in_1[2], in_2);  // AND_Gate
  and and_6 (bgeu, in_1[0], in_1[1], in_1[2], in_2);
  not not_1 (not_1_out, BrEq);
  not not_2 (not_2_out, BrLt);
  Multiplexer #(.enable("false"), .select(3)) multiplexer_1 (
    .in0(1'b0), .in1(BrEq), .in2(not_1_out), .in3(BrLt), .in4(not_2_out), .in5(BrLt), .in6(not_2_out),
    .in7(1'b1), .out(out_6), .sel(priority_encoder_1_out));
  Priority_Encoder priority_encoder_1 (
    .in0(1'b1), .in1(beq), .in2(bne), .in3(blt), .in4(bge), .in5(bltu), .in6(bgeu), .in7(in_5),
    .out(priority_encoder_1_out));  // open: en_in, gs, en_out

  // Other names for the same wires on the sheet: Func3[2:0] = in_1; IsBType = in_2; IsJal = in_5; PCSel = out_6

  // Notes on the sheet:
  //   input
  //   output
endmodule

module LuiDetector (
  input  [6:0] in_1,
  output out_2
);

  and and_1 (out_2, in_1[0], in_1[1], in_1[2], ~in_1[3], in_1[4], in_1[5], ~in_1[6]);  // AND_Gate

  // Other names for the same wires on the sheet: IsLui = out_2; OpCode[6:0] = in_1

  // Notes on the sheet:
  //   input
  //   output
endmodule

module AuipcDetector (
  input  [6:0] in_1,
  output out_2
);

  and and_1 (out_2, in_1[0], in_1[1], in_1[2], ~in_1[3], in_1[4], ~in_1[5], ~in_1[6]);  // AND_Gate

  // Other names for the same wires on the sheet: IsAuipc = out_2; OpCode[6:0] = in_1

  // Notes on the sheet:
  //   input
  //   output
endmodule

module JalDetector (
  input  [6:0] in_1,
  output out_2
);

  and and_1 (out_2, in_1[0], in_1[1], in_1[2], in_1[3], ~in_1[4], in_1[5], in_1[6]);  // AND_Gate

  // Other names for the same wires on the sheet: IsJal = out_2; OpCode[6:0] = in_1

  // Notes on the sheet:
  //   input
  //   output
endmodule

module JalrDetector (
  input  [6:0] in_1,
  output out_2
);

  and and_1 (out_2, in_1[0], in_1[1], in_1[2], ~in_1[3], ~in_1[4], in_1[5], in_1[6]);  // AND_Gate

  // Other names for the same wires on the sheet: IsJalr = out_2; OpCode[6:0] = in_1

  // Notes on the sheet:
  //   input
  //   output
endmodule

module CSRTypeDetector (
  input  [6:0] in_1,
  output out_2
);

  and and_1 (out_2, in_1[0], in_1[1], ~in_1[2], ~in_1[3], in_1[4], in_1[5], in_1[6]);  // AND_Gate

  // Other names for the same wires on the sheet: IsCSRType = out_2; OpCode[6:0] = in_1

  // Notes on the sheet:
  //   input
  //   output
endmodule
