// Logisim project cpu.circ as structural Verilog: 3 circuits, main circuit cpu
module cpu (
  input  clk,
  input  [31:0] INSTRUCTION,
  input  [31:0] READ_DATA,
  output [31:0] WRITE_ADDRESS,
  output [31:0] PROGRAM_COUNTER,
  output [31:0] ra,
  output [31:0] sp,
  output [31:0] t0,
  output [31:0] t1,
  output [31:0] t2,
  output [31:0] s0,
  output [31:0] s1,
  output [31:0] a0,
  output [31:0] tohost,
  output [3:0] WRITE_ENABLE,
  output [31:0] WRITE_DATA
);

  wire ASel, BrEq, BrLt, BrUn, BSel, CSRSel, CSRWen, MemRW, PCSel, RegWEn;
  wire [1:0] MaskType, WBSel;
  wire [2:0] ImmSel;
  wire [3:0] ALUSel;
  wire [31:0] adder_1_out, adder_2_out, IMM, INSTRUCTION_NEXT, MOD_READ_DATA, multiplexer_1_out,
       multiplexer_2_out, multiplexer_3_out, multiplexer_4_out, multiplexer_5_out, PC_NEXT, READ_DATA1,
       READ_DATA2, WB_DATA;

  control_logic control_logic_1 (
    .CSRWen(CSRWen), .out_15(MaskType), .PCSel(PCSel), .RegWEn(RegWEn), .ImmSel(ImmSel), .BrUn(BrUn),
    .ASel(ASel), .BSel(BSel), .ALUSel(ALUSel), .MemRW(MemRW), .WBSel(WBSel), .CSRSel(CSRSel),
    .inst(INSTRUCTION_NEXT), .BrEq(BrEq), .BrLt(BrLt));
  imm_gen imm_gen_1 (.inst(INSTRUCTION_NEXT), .ImmSel(ImmSel), .imm(IMM));
  Adder #(.width(32)) adder_1 (.a(PROGRAM_COUNTER), .b(32'h4), .out(adder_1_out));  // open: cin, cout
  Multiplexer #(.enable("false"), .width(32)) multiplexer_1 (
    .in0(INSTRUCTION), .in1({32{1'b0}}), .out(multiplexer_1_out), .sel(PCSel));
  regfile regfile_1 (
    .rs1(INSTRUCTION_NEXT[19:15]), .rs2(INSTRUCTION_NEXT[24:20]), .rd(INSTRUCTION_NEXT[11:7]),
    .Write_Data(WB_DATA), .RegWEn(RegWEn), .clk(clk), .ra(ra), .sp(sp), .t0(t0), .t1(t1), .t2(t2), .s0(s0),
    .s1(s1), .a0(a0), .Read_Data_1(READ_DATA1), .Read_Data_2(READ_DATA2));
  Multiplexer #(.enable("false"), .width(32)) multiplexer_2 (
    .in0(adder_1_out), .in1(WRITE_ADDRESS), .out(multiplexer_2_out), .sel(PCSel));
  Register #(.width(32)) INSRUCTION_BUFFER (.D(multiplexer_1_out), .clk(clk), .Q(INSTRUCTION_NEXT));  // open: en, clr
  Register #(.width(32)) PC_BUFFER (.D(PROGRAM_COUNTER), .clk(clk), .Q(PC_NEXT));  // open: en, clr
  Register #(.width(32)) PC (.D(multiplexer_2_out), .clk(clk), .Q(PROGRAM_COUNTER));  // open: en, clr
  branch_comp branch_comp_1 (.rs1(READ_DATA1), .rs2(READ_DATA2), .BrUn(BrUn), .BrEq(BrEq), .BrLt(BrLt));
  Multiplexer #(.enable("false"), .width(32)) multiplexer_3 (
    .in0(READ_DATA1), .in1(PC_NEXT), .out(multiplexer_3_out), .sel(ASel));
  Multiplexer #(.enable("false"), .width(32)) multiplexer_4 (
    .in0(READ_DATA2), .in1(IMM), .out(multiplexer_4_out), .sel(BSel));
  alu alu_1 (.Result(WRITE_ADDRESS), .A(multiplexer_3_out), .B(multiplexer_4_out), .ALUSel(ALUSel));
  Multiplexer #(.enable("false"), .width(32)) multiplexer_5 (
    .in0(READ_DATA1), .in1(IMM), .out(multiplexer_5_out), .sel(CSRSel));
  Adder #(.width(32)) adder_2 (.a(PC_NEXT), .b(32'h4), .out(adder_2_out));  // open: cin, cout
  // MemReadDataProcessor memreaddataprocessor_1: pin names not known; wires that end beside it: MemRW, MaskType, READ_DATA, WRITE_ADDRESS, MOD_READ_DATA
  MemWriteDataProcessor memwritedataprocessor_1 (
    .OutData(WRITE_DATA), .out_5(WRITE_ENABLE), .MemRW(MemRW), .MaskType(MaskType), .in_3(READ_DATA2));
  csr csr_1 (.CSR_address(12'h51e), .CSR_din(multiplexer_5_out), .CSR_WE(CSRWen), .clk(clk), .tohost(tohost));
  Multiplexer #(.enable("false"), .select(2), .width(32)) multiplexer_6 (
    .in0(WRITE_ADDRESS), .in1(MOD_READ_DATA), .in2(adder_2_out), .out(WB_DATA), .sel(WBSel));  // open: in3

  // Other names for the same wires on the sheet: ALUResult[31:0] = WRITE_ADDRESS

  // Notes on the sheet:
  //   Output to IMEM
  //   IMEM (do **NOT** move this)
  //   Inputs from IMEM
  //   It is OK to move the PC, RegFile, ALU, MEM, Branch Comp, Imm Gen, and Control Logic to wherever is most convenient for you when constructing your CPU, and to delete this text
  //   Inputs/Outputs for testing. Do **NOT** move these.
  //   Outputs To DMEM
  //   DMEM (do **NOT** move this)
  //   Inputs From DMEM
endmodule

module MemReadDataProcessor (
  input  MemRW,
  input  [1:0] MaskType,
  input  [31:0] in_3,
  output [31:0] OutData
);

  wire ByteFlag, HalfFlag, WordFlag;
  wire [1:0] priority_encoder_1_out;
  wire [31:0] OutByte, OutHalfWord;

  assign OutByte = {{24{in_3[7]}}, in_3[7:0]};  // Bit_Extender bit_extender_1
  assign OutHalfWord = {{16{in_3[15]}}, in_3[15:0]};  // Bit_Extender bit_extender_2
  Multiplexer #(.enable("false"), .select(2), .width(32)) multiplexer_1 (
    .in0(in_3), .in1(in_3), .in2(OutHalfWord), .in3(OutByte), .out(OutData), .sel(priority_encoder_1_out));
  Priority_Encoder #(.select(2)) priority_encoder_1 (
    .in0(1'b1), .in1(WordFlag), .in2(HalfFlag), .in3(ByteFlag), .out(priority_encoder_1_out));  // open: gs, en_out, en_in
  and and_1 (ByteFlag, ~MemRW, MaskType[0], ~MaskType[1]);  // AND_Gate
  and and_2 (HalfFlag, ~MemRW, ~MaskType[0], MaskType[1]);  // AND_Gate
  and and_3 (WordFlag, ~MemRW, MaskType[0], MaskType[1]);  // AND_Gate

  // Other names for the same wires on the sheet: Byte0[7:0] = in_3[7:0]; HalfWord[15:0] = in_3[15:0];
  //   READ_DATA[31:0] = in_3

  // Notes on the sheet:
  //   INPUTS to your circuit
  //   OUTPUT from your circuit
endmodule

module MemWriteDataProcessor (
  input  MemRW,
  input  [1:0] MaskType,
  input  [31:0] in_3,
  output [31:0] OutData,
  output [3:0] out_5
);

  wire WriteByte, WriteHalfWord, WriteWord;
  wire [1:0] WriteMask;
  wire [31:0] OutWriteByte, OutWriteHalfWord;

  and and_1 (WriteByte, MaskType[0], ~MaskType[1], MemRW);  // AND_Gate
  and and_2 (WriteHalfWord, ~MaskType[0], MaskType[1], MemRW);  // AND_Gate
  and and_3 (WriteWord, MaskType[0], MaskType[1], MemRW);
  assign OutWriteByte = {{24{1'b0}}, in_3[7:0]};  // Bit_Extender bit_extender_1
  assign OutWriteHalfWord = {{16{1'b0}}, in_3[15:0]};  // Bit_Extender bit_extender_2
  Priority_Encoder #(.select(2)) priority_encoder_1 (
    .in0(1'b1), .in1(WriteByte), .in2(WriteHalfWord), .in3(WriteWord), .out(WriteMask));  // open: gs, en_out, en_in
  Multiplexer #(.enable("false"), .select(2), .width(4)) multiplexer_1 (
    .in0(4'b0000), .in1(4'b0001), .in2(4'b0011), .in3(4'b1111), .out(out_5), .sel(WriteMask));
  Multiplexer #(.enable("false"), .select(2), .width(32)) multiplexer_2 (
    .in0({32{1'b0}}), .in1(OutWriteByte), .in2(OutWriteHalfWord), .in3(in_3), .out(OutData), .sel(MaskType));

  // Other names for the same wires on the sheet: TypeBit0 = MaskType[0]; TypeBit1 = MaskType[1];
  //   OutWriteData[31:0] = OutData; Byte[7:0] = in_3[7:0]; HalfWord[15:0] = in_3[15:0]; WRITE_DATA[31:0] = in_3;
  //   WRITE_ENABLE[3:0] = out_5

  // Notes on the sheet:
  //   INPUTS to your circuit
  //   OUTPUT from your circuit
endmodule
