// Logisim project regfile.circ as structural Verilog: 1 circuit, main circuit regfile
module regfile (
  input  [4:0] rs1,
  input  [4:0] rs2,
  input  [4:0] rd,
  input  [31:0] Write_Data,
  input  RegWEn,
  input  clk,
  output [31:0] ra,
  output [31:0] sp,
  output [31:0] t0,
  output [31:0] t1,
  output [31:0] t2,
  output [31:0] s0,
  output [31:0] s1,
  output [31:0] a0,
  output [31:0] Read_Data_1,
  output [31:0] Read_Data_2
);

  wire write_en0, write_en1, write_en2, write_en3, write_en4, write_en5, write_en6, write_en7, write_en8,
       write_en9, write_en10, write_en11, write_en12, write_en13, write_en14, write_en15, write_en16,
       write_en17, write_en18, write_en19, write_en20, write_en21, write_en22, write_en23, write_en24,
       write_en25, write_en26, write_en27, write_en28, write_en29, write_en30, write_en31;
  wire [31:0] reg_0_data, reg_3_data, reg_4_data, reg_11_data, reg_12_data, reg_13_data, reg_14_data,
       reg_15_data, reg_16_data, reg_17_data, reg_18_data, reg_19_data, reg_20_data, reg_21_data,
       reg_22_data, reg_22data, reg_23_data, reg_24_data, reg_25_data, reg_26_data, reg_27_data, reg_28_data,
       reg_29_data, reg_30_data, reg_31_data;

  Demultiplexer #(.enable("false"), .select(5)) demultiplexer_1 (
    .out0(write_en0), .out1(write_en1), .out2(write_en2), .out3(write_en3), .out4(write_en4),
    .out5(write_en5), .out6(write_en6), .out7(write_en7), .out8(write_en8), .out9(write_en9),
    .out10(write_en10), .out11(write_en11), .out12(write_en12), .out13(write_en13), .out14(write_en14),
    .out15(write_en15), .out16(write_en16), .out17(write_en17), .out18(write_en18), .out19(write_en19),
    .out20(write_en20), .out21(write_en21), .out22(write_en22), .out23(write_en23), .out24(write_en24),
    .out25(write_en25), .out26(write_en26), .out27(write_en27), .out28(write_en28), .out29(write_en29),
    .out30(write_en30), .out31(write_en31), .in(RegWEn), .sel(rd));
  Register #(.width(32)) register_1 (.D(Write_Data), .en(write_en0), .clk(clk), .Q(reg_0_data), .clr(1'b1));
  Register #(.width(32)) register_2 (.D(Write_Data), .en(write_en4), .clk(clk), .Q(reg_4_data));  // open: clr
  Register #(.width(32)) register_3 (.D(Write_Data), .en(write_en8), .clk(clk), .Q(s0));  // open: clr
  Register #(.width(32)) register_4 (.D(Write_Data), .en(write_en12), .clk(clk), .Q(reg_12_data));  // open: clr
  Register #(.width(32)) register_5 (.D(Write_Data), .en(write_en16), .clk(clk), .Q(reg_16_data));  // open: clr
  Register #(.width(32)) register_6 (.D(Write_Data), .en(write_en20), .clk(clk), .Q(reg_20_data));  // open: clr
  Register #(.width(32)) register_7 (.D(Write_Data), .en(write_en24), .clk(clk), .Q(reg_24_data));  // open: clr
  Register #(.width(32)) register_8 (.D(Write_Data), .en(write_en28), .clk(clk), .Q(reg_28_data));  // open: clr
  Register #(.width(32)) register_9 (.D(Write_Data), .en(write_en1), .clk(clk), .Q(ra));  // open: clr
  Register #(.width(32)) register_10 (.D(Write_Data), .en(write_en5), .clk(clk), .Q(t0));  // open: clr
  Register #(.width(32)) register_11 (.D(Write_Data), .en(write_en9), .clk(clk), .Q(s1));  // open: clr
  Register #(.width(32)) register_12 (.D(Write_Data), .en(write_en13), .clk(clk), .Q(reg_13_data));  // open: clr
  Register #(.width(32)) register_13 (.D(Write_Data), .en(write_en17), .clk(clk), .Q(reg_17_data));  // open: clr
  Register #(.width(32)) register_14 (.D(Write_Data), .en(write_en21), .clk(clk), .Q(reg_21_data));  // open: clr
  Register #(.width(32)) register_15 (.D(Write_Data), .en(write_en25), .clk(clk), .Q(reg_25_data));  // open: clr
  Register #(.width(32)) register_16 (.D(Write_Data), .en(write_en29), .clk(clk), .Q(reg_29_data));  // open: clr
  Register #(.width(32)) register_17 (.D(Write_Data), .en(write_en2), .clk(clk), .Q(sp));  // open: clr
  Register #(.width(32)) register_18 (.D(Write_Data), .en(write_en6), .clk(clk), .Q(t1));  // open: clr
  Register #(.width(32)) register_19 (.D(Write_Data), .en(write_en10), .clk(clk), .Q(a0));  // open: clr
  Register #(.width(32)) register_20 (.D(Write_Data), .en(write_en14), .clk(clk), .Q(reg_14_data));  // open: clr
  Register #(.width(32)) register_21 (.D(Write_Data), .en(write_en18), .clk(clk), .Q(reg_18_data));  // open: clr
  Register #(.width(32)) register_22 (.D(Write_Data), .en(write_en22), .clk(clk), .Q(reg_22data));  // open: clr
  Register #(.width(32)) register_23 (.D(Write_Data), .en(write_en26), .clk(clk), .Q(reg_26_data));  // open: clr
  Register #(.width(32)) register_24 (.D(Write_Data), .en(write_en30), .clk(clk), .Q(reg_30_data));  // open: clr
  Multiplexer #(.enable("false"), .select(5), .width(32)) multiplexer_1 (
    .in0(reg_0_data), .in1(ra), .in2(sp), .in3(reg_3_data), .in4(reg_4_data), .in5(t0), .in6(t1), .in7(t2),
    .in8(s0), .in9(s1), .in10(a0), .in11(reg_11_data), .in12(reg_12_data), .in13(reg_13_data),
    .in14(reg_14_data), .in15(reg_15_data), .in16(reg_16_data), .in17(reg_17_data), .in18(reg_18_data),
    .in19(reg_19_data), .in20(reg_20_data), .in21(reg_21_data), .in22(reg_22_data), .in23(reg_23_data),
    .in24(reg_24_data), .in25(reg_25_data), .in26(reg_26_data), .in27(reg_27_data), .in28(reg_28_data),
    .in29(reg_29_data), .in30(reg_30_data), .in31(reg_31_data), .out(Read_Data_1), .sel(rs1));
  Register #(.width(32)) register_25 (.D(Write_Data), .en(write_en3), .clk(clk), .Q(reg_3_data));  // open: clr
  Register #(.width(32)) register_26 (.D(Write_Data), .en(write_en7), .clk(clk), .Q(t2));  // open: clr
  Register #(.width(32)) register_27 (.D(Write_Data), .en(write_en11), .clk(clk), .Q(reg_11_data));  // open: clr
  Register #(.width(32)) register_28 (.D(Write_Data), .en(write_en15), .clk(clk), .Q(reg_15_data));  // open: clr
  Register #(.width(32)) register_29 (.D(Write_Data), .en(write_en19), .clk(clk), .Q(reg_19_data));  // open: clr
  Register #(.width(32)) register_30 (.D(Write_Data), .en(write_en23), .clk(clk), .Q(reg_23_data));  // open: clr
  Register #(.width(32)) register_31 (.D(Write_Data), .en(write_en27), .clk(clk), .Q(reg_27_data));  // open: clr
  Register #(.width(32)) register_32 (.D(Write_Data), .en(write_en31), .clk(clk), .Q(reg_31_data));  // open: clr
  Multiplexer #(.enable("false"), .select(5), .width(32)) multiplexer_2 (
    .in0(reg_0_data), .in1(ra), .in2(sp), .in3(reg_3_data), .in4(reg_4_data), .in5(t0), .in6(t1), .in7(t2),
    .in8(s0), .in9(s1), .in10(a0), .in11(reg_11_data), .in12(reg_12_data), .in13(reg_13_data),
    .in14(reg_14_data), .in15(reg_15_data), .in16(reg_16_data), .in17(reg_17_data), .in18(reg_18_data),
    .in19(reg_19_data), .in20(reg_20_data), .in21(reg_21_data), .in22(reg_22_data), .in23(reg_23_data),
    .in24(reg_24_data), .in25(reg_25_data), .in26(reg_26_data), .in27(reg_27_data), .in28(reg_28_data),
    .in29(reg_29_data), .in30(reg_30_data), .in31(reg_31_data), .out(Read_Data_2), .sel(rs2));

  // Other names for the same wires on the sheet: read_data1[31:0] = Read_Data_1; read_data2[31:0] = Read_Data_2;
  //   read_reg1[4:0] = rs1; read_reg2[4:0] = rs2; reg_1_data[31:0] = ra; reg_2_data[31:0] = sp; reg_5_data[31:0] = t0;
  //   reg_6_data[31:0] = t1; reg_7_data[31:0] = t2; reg_8_data[31:0] = s0; reg_9_data[31:0] = s1;
  //   reg_10_data[31:0] = a0; write_en = RegWEn; write_reg[4:0] = rd; x0[31:0] = reg_0_data

  // Notes on the sheet:
  //   INPUTS to your circuit
  //   DON'T CHANGE THE LOCATIONS OF THE INPUTS AND OUTPUTS!
  //   These are DEBUG/TEST outputs from your circuit.
  //   OUTPUTS from your circuit
endmodule
