// Logisim project cpu-bgeu.circ as structural Verilog: 1 circuit, main circuit run_main
module run_main (
  output [31:0] ra,
  output [31:0] sp,
  output [31:0] t0,
  output [31:0] t1,
  output [31:0] t2,
  output [31:0] s0,
  output [31:0] s1,
  output [31:0] a0,
  output [31:0] Requested_Address,
  output [31:0] Requested_Instruction,
  output [15:0] Time_Step,
  output halt
);

  wire clk;

  Clock clock_1 (.out(clk));
  // Probe on Requested_Address
  // test_harness test_harness_1: pin names not known; wires that end beside it: Requested_Instruction, clk, Requested_Address, ra, sp, t0, t1, t2, s0, s1, a0
  ROM #(.addrWidth(14), .dataWidth(32)) rom_1 (.addr(Requested_Address[15:2]), .data(Requested_Instruction));
  // Probe on Requested_Instruction
  Counter #(.max('hffff), .width(16)) counter_1 (.clk(clk), .Q(Time_Step));  // open: clr, load, up, count, D, carry
  Comparator #(.width(16)) comparator_1 (.a(Time_Step), .b(16'he), .eq(halt));  // open: gt, lt

  // Other names for the same wires on the sheet: fetch_addr[31:0] = Requested_Address;
  //   Instruction[31:0] = Requested_Instruction

  // Notes on the sheet:
  //   contents of rom_1 (hex, n*v repeats v):
  //   06400413 06300493 00947863 00100413 00140413 00140413 00100493 00100493 01E49493 00100413 01F49493
  //   00947863 00100293 00100313 00100393 00200493
  //   Instruction Memory
  //   Halts Execution After Constant # of Clock Cycles
  //   Constant
endmodule
