// Logisim project ex5.circ as structural Verilog: 5 circuits, main circuit rotr
module rotr (
  input  [15:0] A,
  input  [3:0] B,
  output [15:0] Out1
);

  wire [15:0] r1, r2, r4, rot1_1_out_2, rot2_1_out_2, rot4_1_out_2, rot8_1_out_2;

  rot1 rot1_1 (.in_1(A), .out_2(rot1_1_out_2));
  rot2 rot2_1 (.in_1(r1), .out_2(rot2_1_out_2));
  rot4 rot4_1 (.in_1(r2), .out_2(rot4_1_out_2));
  rot8 rot8_1 (.in_1(r4), .out_2(rot8_1_out_2));
  Multiplexer #(.enable("false"), .width(16)) multiplexer_1 (.in0(A), .in1(rot1_1_out_2), .out(r1), .sel(B[0]));
  Multiplexer #(.enable("false"), .width(16)) multiplexer_2 (.in0(r1), .in1(rot2_1_out_2), .out(r2), .sel(B[1]));
  Multiplexer #(.enable("false"), .width(16)) multiplexer_3 (.in0(r2), .in1(rot4_1_out_2), .out(r4), .sel(B[2]));
  Multiplexer #(.enable("false"), .width(16)) multiplexer_4 (.in0(r4), .in1(rot8_1_out_2), .out(Out1), .sel(B[3]));

  // Other names for the same wires on the sheet: i[15:0] = A; q[15:0] = Out1

  // Notes on the sheet:
  //   PUT CIRCUITRY HERE
endmodule

module rot8 (
  input  [15:0] in_1,
  output [15:0] out_2
);

  wire [15:0] rot4_1_out_2;

  rot4 rot4_1 (.in_1(in_1), .out_2(rot4_1_out_2));
  rot4 rot4_2 (.in_1(rot4_1_out_2), .out_2(out_2));

  // Notes on the sheet:
  //   PUT CIRCUITRY HERE
endmodule

module rot4 (
  input  [15:0] in_1,
  output [15:0] out_2
);

  wire [15:0] rot2_1_out_2;

  rot2 rot2_1 (.in_1(in_1), .out_2(rot2_1_out_2));
  rot2 rot2_2 (.in_1(rot2_1_out_2), .out_2(out_2));

  // Notes on the sheet:
  //   PUT CIRCUITRY HERE
endmodule

module rot2 (
  input  [15:0] in_1,
  output [15:0] out_2
);

  wire [15:0] rot1_1_out_2;

  rot1 rot1_1 (.in_1(in_1), .out_2(rot1_1_out_2));
  rot1 rot1_2 (.in_1(rot1_1_out_2), .out_2(out_2));

  // Notes on the sheet:
  //   PUT CIRCUITRY HERE
endmodule

module rot1 (
  input  [15:0] in_1,
  output [15:0] out_2
);


  assign out_2 = {in_1[0], in_1[15:1]};

  // Notes on the sheet:
  //   PUT CIRCUITRY HERE
endmodule
